// Logisim project v5 Main 18 bit.circ as structural Verilog: 1 circuit, main circuit main
module main (
  input  in_1,
  input  in_2,
  input  in_3,
  input  in_4,
  input  in_5,
  input  in_6,
  input  in_7,
  output [17:0] Instructions,
  output [3:0] RD__Immediate,
  output [3:0] RT,
  output [3:0] RS,
  output [17:0] Data_Read_2,
  output [3:0] OP,
  output [17:0] Output,
  output [1:0] Function,
  output [17:0] Data_Read_1,
  output [17:0] Address,
  output [17:0] Instructions_2,
  output [7:0] out_19,
  output [17:0] overflow
);

  wire and_1_out, bit_extender_7_out, clk, cu_aluClt, lw, main_2_zero, main_3_cu_bne, R_D, R_I, R_W, Res_Mem,
       sl, sw;
  wire [1:0] AluOp;
  wire [2:0] bit_extender_6_out, multiplexer_4_out;
  wire [3:0] multiplexer_2_out;
  wire [6:0] adder_1_out, adder_2_out, bit_extender_1_out, bit_extender_2_out, shifter_1_out, shifter_2_out;
  wire [7:0] bit_extender_3_out, bit_extender_4_out;
  wire [17:0] adder_3_out, Address_t, bit_extender_5_out, cu_bne, main_4_out_7, multiplexer_3_out,
       multiplexer_5_out, ram_1_data, register_1_q, shifter_3_out, shifter_5_out;

  assign bit_extender_1_out = {{3{1'b0}}, Instructions_2[3:0]};  // Bit_Extender bit_extender_1
  assign bit_extender_2_out = {{5{1'b0}}, Function};  // Bit_Extender bit_extender_2
  Register #(.width(18)) register_1 (.D(Address_t), .Q(register_1_q), .clk(clk), .clr(in_4));  // open: en
  Clock clock_1 (.out(clk));
  Shifter #(.width(7)) shifter_1 (.in(bit_extender_1_out), .\dist (3'b100), .out(shifter_1_out));
  Shifter #(.width(7)) shifter_2 (.in(7'b0000011), .\dist (3'b101), .out(shifter_2_out));
  Adder #(.width(7)) adder_1 (.a(shifter_1_out), .b(bit_extender_2_out), .out(adder_1_out));  // open: cin, cout
  Adder #(.width(7)) adder_2 (.a(shifter_2_out), .b(7'b0000100), .out(adder_2_out));  // open: cin, cout
  Adder #(.width(18)) adder_3 (.a(register_1_q), .b(18'h1), .out(adder_3_out));  // open: cin, cout
  ROM #(.addrWidth(18), .dataWidth(18)) rom_1 (
    .addr(register_1_q), .data({Function, Instructions_2[15:0]}));  // open: sel
  assign bit_extender_3_out = {{1{1'b0}}, adder_1_out};  // Bit_Extender bit_extender_3
  assign bit_extender_4_out = {{1{1'b0}}, adder_2_out};  // Bit_Extender bit_extender_4
  Multiplexer #(.width(8), .enable("false")) multiplexer_1 (
    .in0(bit_extender_3_out), .in1(bit_extender_4_out), .out(out_19), .sel(in_6));
  Shifter #(.width(18), .shift("lr")) shifter_3 (
    .in({Function, 4'b0000, Instructions_2[11:0]}), .\dist (5'b01001), .out(shifter_3_out));
  Shifter #(.width(18), .shift("lr")) shifter_4 (.in(shifter_3_out), .\dist (5'b00101), .out(Instructions));
  Multiplexer #(.width(4), .enable("false")) multiplexer_2 (
    .in0(Instructions_2[7:4]), .in1(Instructions_2[3:0]), .out(multiplexer_2_out), .sel(R_D));
  assign bit_extender_5_out = {{10{1'b0}}, out_19};  // Bit_Extender bit_extender_5
  // v3_REG_18_bit__main main_1: pin names not known; wires that end beside it: Instructions_2[11:8], Instructions_2[7:4], multiplexer_2_out, Output, clk, R_W, Data_Read_1, Data_Read_2
  assign bit_extender_6_out = {{1{1'b0}}, Function};  // Bit_Extender bit_extender_6
  Multiplexer #(.width(18), .enable("false")) multiplexer_3 (
    .in0(Data_Read_2), .in1(bit_extender_5_out), .out(multiplexer_3_out), .sel(R_I));
  Multiplexer #(.width(3), .enable("false")) multiplexer_4 (
    .in0(bit_extender_6_out), .in1({in_7, AluOp}), .out(multiplexer_4_out), .sel(cu_aluClt));
  Shifter #(.width(18)) shifter_5 (.in(bit_extender_5_out), .\dist (5'b00001), .out(shifter_5_out));
  Bit_Extender #(.in_width(18), .out_width(1)) bit_extender_7 (.in(cu_bne), .out(bit_extender_7_out));
  v4_ALU_18_bit_main main_2 (
    .ZERO(main_2_zero), .out_7(Address), .overflow_sum(overflow), .c_in(in_2), .A(Data_Read_1),
    .B(multiplexer_3_out), .OP_code(multiplexer_4_out));  // open: sum_carry, c_in_sub, sub_carry
  and and_1 (and_1_out, bit_extender_7_out, main_2_zero);
  v4_Control_Unit_main main_3 (
    .A(Instructions_2[13]), .B(Instructions_2[12]), .R_D(R_D), .R_W(R_W), .SW(sw), .SL(sl), .LW(lw),
    .Res_Mem(Res_Mem), ._1(1'b1), .ALU_OP1(AluOp[1]), .Cu_BNE(main_3_cu_bne), .Cu_aluClt(cu_aluClt),
    .ALU_OP0(AluOp[0]), .R_I(R_I));
  v4_ALU_18_bit_main main_4 (
    .out_7(main_4_out_7), .c_in(in_1), .A(adder_3_out), .B(shifter_5_out), .OP_code(3'b010));  // open: ZERO, overflow_sum, sum_carry, c_in_sub, sub_carry
  assign cu_bne = {{17{1'b0}}, main_3_cu_bne};  // Bit_Extender bit_extender_8
  Multiplexer #(.width(18), .enable("false")) multiplexer_5 (
    .in0(adder_3_out), .in1(main_4_out_7), .out(multiplexer_5_out), .sel(and_1_out));
  Multiplexer #(.width(18), .enable("false")) multiplexer_6 (
    .in0(Address), .in1(ram_1_data), .out(Output), .sel(Res_Mem));
  RAM #(.addrWidth(18), .dataWidth(18), .bus("separate")) ram_1 (
    .addr(Address), .din(Data_Read_2), .data(ram_1_data), .str(sw), .sel(sl), .clk(clk), .ld(lw), .clr(in_3));
  Multiplexer #(.width(18), .enable("false")) multiplexer_7 (
    .in0(multiplexer_5_out), .in1(Instructions), .out(Address_t), .sel(in_5));

  assign Instructions_2[17:16] = Function;
  assign OP = Instructions_2[15:12];
  assign RD__Immediate = Instructions_2[3:0];
  assign RS = Instructions_2[11:8];
  assign RT = Instructions_2[7:4];

  // Other names for the same wires on the sheet: RD[3:0] = Instructions_2[3:0]; AluOp[2] = in_7; D_in[17:0] = Output;
  //   Imm[7:0] = out_19; cu_[3:0] = Instructions_2[15:12]; J = in_5

  // Notes on the sheet:
  //   RD-3 , Fun - 3 for 61
  //   contents of rom_1 (hex, n*v repeats v):
  //   12302 3230 10210 0 23230 10000 32400 0 0 30003
  //   or maybe , fix the 100 data on R4 beforehand
  //   need 2 bew for adding this into control unit
  //   update- no need , we can store the data anyway
  //   for 100 , keep this 1
endmodule
